# Fritzing sketch Raspberry Control Panel (saved by Fritzing 0.9.3b)
breadboards: 1

parts:
  Raspberry_Pi_1 = Raspberry Pi 3 [part_number=RPI-3-V1.2]
  S3 = Round Pushbutton
  S4 = Round Pushbutton
  LED3 = smd LED [color="Red (633nm)" package="0805 [SMD]"]
  LED4 = smd LED [color="Red (633nm)" package="0805 [SMD]"]
  R4 = Resistor [tolerance=±5% resistance=220 package="0402 [SMD]"]
  R5 = Resistor [tolerance=±5% resistance=470 package="0402 [SMD]"]
  R6 = Resistor [tolerance=±5% resistance=2.2k package="0402 [SMD]"]

nets:
  N1: Raspberry_Pi_1.3v3, LED3.anode, R6.Pin_1
  N2: Raspberry_Pi_1.GPIO21, S3.leg1
  N3: Raspberry_Pi_1.GPIO20, S4.leg1
  N4: Raspberry_Pi_1.GPIO16, LED4.cathode
  N5: Raspberry_Pi_1.GND, R4.Pin_1, R5.Pin_1
  N6: S3.leg0, LED3.cathode, R5.Pin_0
  N7: S4.leg0, R6.Pin_0
